# Fritzing sketch Debouncer (saved by Fritzing 0.9.3b)
breadboards: 1

parts:
  S1 = Pushbutton [package="[THT]"]
  R1 = Resistor [tolerance=±5% resistance=100k package=THT]
  R2 = Resistor [tolerance=±5% resistance=10k package=THT]
  C1 = Ceramic Capacitor [capacitance=100nF part_number=104 package="100 mil [THT, multilayer]"]
  S2 = Pushbutton [package="[THT]"]
  R3 = Resistor [tolerance=±5% resistance=10k package=THT]
  R4 = Resistor [tolerance=±5% resistance=100k package=THT]
  C2 = Ceramic Capacitor [capacitance=100nF part_number=104 voltage=6.3V package="100 mil [THT, multilayer]"]
  J1 = female pin header, 2 pins [form="♀ (female)"]
  J2 = female pin header, 2 pins [form="♀ (female)"]
  Power_plug1 = Power plug [part_number=5v]

nets:
  N1: S1.Pin_1, S1.Pin_2, R1.Pin_0, R2.Pin_0
  N2: S1.Pin_3, S1.Pin_4, R3.Pin_0, Power_plug1.VCC
  N3: R1.Pin_1, C1.1, S2.Pin_1, S2.Pin_2, C2.0, J1.pin2, J2.pin1, Power_plug1.GND
  N4: R2.Pin_1, C1.0
  N5: S2.Pin_3, S2.Pin_4, R3.Pin_1, R4.Pin_1
  N6: R4.Pin_0, C2.1

notes:
  Debounce
  High Push Button
  Debounce
  Low Push Button
  I/O Pin
  100nf / 0.1uf
  5V Power
  To remove the small ripple of current that forms when a mechanical switch is pushed in an electrical circuit and makes a series of short contacts.
