# Fritzing sketch 8BitMicroController (saved by Fritzing 0.9.3b)
breadboards: 5

parts:
  Power_plug_2_-_6_v1 = Power plug [part_number="2v - 6 v Power"]
  J2_Output_Pin1 = female pin header, 9 pins [form="♀ (female)"]
  S2_Clear_|_Write1 = Toggle Switch [part_number="Clear | Write Swich" package=THT]
  S1_Display_|_None1 = Toggle Switch [part_number="Display Swich" package=THT]
  J1_Control1 = female pin header, 5 pins [form="♀ (female)" part_number="Control Pin"]
  U1_8Bit_Register1 = 74HC595 [part_number="8 Bit Shift Register" package="DIP16 [THT]"]
  S5 = Pushbutton [package="[THT]"]
  R9 = Resistor [tolerance=±5% resistance=10k package=THT]
  R10 = Resistor [tolerance=±5% resistance=100k package=THT]
  C5 = Ceramic Capacitor [capacitance=100nF part_number=104 package="100 mil [THT, multilayer]"]
  J5 = female pin header, 2 pins [form="♀ (female)"]
  S6 = Pushbutton [package="[THT]"]
  R11 = Resistor [tolerance=±5% resistance=100k package=THT]
  R12 = Resistor [tolerance=±5% resistance=10k package=THT]
  C6 = Ceramic Capacitor [capacitance=100nF part_number=104 package="100 mil [THT, multilayer]"]
  J6 = female pin header, 2 pins [form="♀ (female)"]
  S7 = Pushbutton [package="[THT]"]
  R13 = Resistor [tolerance=±5% resistance=100k package=THT]
  R14 = Resistor [tolerance=±5% resistance=10k package=THT]
  C7 = Ceramic Capacitor [capacitance=100nF part_number=104 package="100 mil [THT, multilayer]"]
  J7 = female pin header, 2 pins [form="♀ (female)"]
  Digit_2 = 7 Segment Display
  R15 = Resistor [tolerance=±5% resistance=220 package=THT]

nets:
  GND: Power_plug_2_-_6_v1.GND, S2_Clear_|_Write1.L1, S1_Display_|_None1.L2, J1_Control1.pin4, U1_8Bit_Register1.GND, R10.Pin_1, C5.1, J5.pin1, R11.Pin_1, C6.1, J6.pin1, R13.Pin_1, C7.1, J7.pin1, R15.Pin_1
  VCC: Power_plug_2_-_6_v1.VCC, S2_Clear_|_Write1.L2, J1_Control1.pin5, U1_8Bit_Register1.VCC, S5.Pin_3, S6.Pin_3, S6.Pin_4, S7.Pin_3
  N1: J2_Output_Pin1.pin1, U1_8Bit_Register1.Q7'
  N2: J2_Output_Pin1.pin2, U1_8Bit_Register1.Q0, Digit_2.Segment_A
  N3: J2_Output_Pin1.pin3, U1_8Bit_Register1.Q1, Digit_2.Segment_B
  N4: J2_Output_Pin1.pin4, U1_8Bit_Register1.Q2, Digit_2.Segment_C
  N5: J2_Output_Pin1.pin5, U1_8Bit_Register1.Q3, Digit_2.Segment_D
  N6: J2_Output_Pin1.pin6, U1_8Bit_Register1.Q4, Digit_2.Segment_E
  N7: J2_Output_Pin1.pin7, U1_8Bit_Register1.Q5, Digit_2.Segment_F
  N8: J2_Output_Pin1.pin8, U1_8Bit_Register1.Q6, Digit_2.Segment_G
  N9: J2_Output_Pin1.pin9, U1_8Bit_Register1.Q7, Digit_2.Segment_DP
  N10: S2_Clear_|_Write1.COM, U1_8Bit_Register1.MR
  N11: S1_Display_|_None1.COM, U1_8Bit_Register1.OE
  N12: J1_Control1.pin1, U1_8Bit_Register1.DS
  N13: J1_Control1.pin2, U1_8Bit_Register1.ST_CP
  N14: J1_Control1.pin3, U1_8Bit_Register1.SH_CP, J6.pin2
  N15: S5.Pin_1, S5.Pin_2, R9.Pin_0, R10.Pin_0
  N16: R9.Pin_1, C5.0
  N17: S6.Pin_1, S6.Pin_2, R11.Pin_0, R12.Pin_0
  N18: R12.Pin_1, C6.0
  N19: S7.Pin_1, S7.Pin_2, R13.Pin_0, R14.Pin_0
  N20: R14.Pin_1, C7.0
  N21: Digit_2.common_cathode, R15.Pin_0

notes:
  Min 2v - Max 6v Power
  74HC595
  Data | Register | Clock | GND | VCC
  Control Buttons Pin And Power
  Display OFF | Display ON
  Clear |  Write
  Output Pin
  SO | A | B | C | D | E | F | G | H
  I/O Pin
  5V Power
  100nf / 0.1uf
  Push Bututon
  MainBoard
  Screen
  Keyboard
  Register Push Button
  With Debounce Filter
  Clock Push Button
  With Debounce Filter
  Data Push Button
  With Debounce Filter
  8 Bit Register
  Segment Display
  MicroController [ Micro Computer :) ]
  Program Guide
  F
  0 1 1 1 0 0 0 1
  REGISTER BUTTON STATE [ Step 3 ]
  CLOCK BUTTON STATE [ Step 2  ]
  FLAG
  DATA BUTTON STATE [ Step 1 ]
  Press
  0
  -
  1
