# Fritzing sketch Register8Bit (saved by Fritzing 0.9.3b)
circuit board: 12.7455cm x 7.17431cm
breadboards: 1

parts:
  S2_Clear_|_Write = Toggle Switch [part_number="Clear | Write Swich" package=THT]
  J1_Control = female pin header, 5 pins [form="♀ (female)" part_number="Control Pin"]
  U1_8Bit_Register = 74HC595 [part_number="8 Bit Shift Register" package="DIP16 [THT]"]
  J2_Output_Pin = female pin header, 9 pins [form="♀ (female)"]
  Power_plug_2_-_6_v = Power plug [part_number="2v - 6 v Power"]
  S1_Display_|_None = Toggle Switch [part_number="Display Swich" package=THT]

nets (from the breadboard view):
  GND: S2_Clear_|_Write.L1, J1_Control.pin4, U1_8Bit_Register.GND, Power_plug_2_-_6_v.GND, S1_Display_|_None.L2
  N1: S2_Clear_|_Write.COM, U1_8Bit_Register.MR
  VCC: S2_Clear_|_Write.L2, J1_Control.pin5, U1_8Bit_Register.VCC, Power_plug_2_-_6_v.VCC
  N2: J1_Control.pin1, U1_8Bit_Register.DS
  N3: J1_Control.pin2, U1_8Bit_Register.ST_CP
  N4: J1_Control.pin3, U1_8Bit_Register.SH_CP
  N5: U1_8Bit_Register.Q1, J2_Output_Pin.pin3
  N6: U1_8Bit_Register.Q2, J2_Output_Pin.pin4
  N7: U1_8Bit_Register.Q3, J2_Output_Pin.pin5
  N8: U1_8Bit_Register.Q4, J2_Output_Pin.pin6
  N9: U1_8Bit_Register.Q5, J2_Output_Pin.pin7
  N10: U1_8Bit_Register.Q6, J2_Output_Pin.pin8
  N11: U1_8Bit_Register.Q7, J2_Output_Pin.pin9
  N12: U1_8Bit_Register.Q7', J2_Output_Pin.pin1
  N13: U1_8Bit_Register.OE, S1_Display_|_None.COM
  N14: U1_8Bit_Register.Q0, J2_Output_Pin.pin2

notes:
  Clear |  Write
  Display OFF | Display ON
  Control Buttons Pin And Power
  Register 8 Bit Shift
  Data | Register | Clock | GND | VCC
  Output Pin
  SO | A | B | C | D | E | F | G | H
  74HC595
  Min 2v - Max 6v Power
