# Fritzing sketch Timer (saved by Fritzing 0.9.3b)
circuit board: 9.09582cm x 5.6321cm
breadboards: 1

parts:
  U1 = 555 Timer [package="DIP8 [THT]"]
  VCC1 = 4 x AAA Battery Mount
  C1 = Electrolytic Capacitor [capacitance=47µF package="100 mil [THT, electrolytic]"]
  LED1 = LED - 5mm [color="Red (633nm)" package="5 mm [THT]"]
  R1 = Resistor [tolerance=±5% resistance=10k package=THT]
  R2 = Resistor [tolerance=±5% resistance=330 part_number=10K package=THT]

nets:
  N1: U1.Ground, VCC1.-, C1.-, LED1.cathode
  N2: U1.Trigger, U1.Threshold, C1.+, R2.Pin_0
  N3: U1.Output, LED1.anode
  N4: U1.Discharge, R1.Pin_1, R2.Pin_1
  N5: U1.Vcc_Supply_Voltage, VCC1.+, R1.Pin_0
